# Fritzing sketch schematics (saved by Fritzing 0.9.3b)
breadboards: 1

parts:
  U1 = ESP8266 NodeMCU LoLin module
  IR1 = TSOP312.., 314.. [package=THT]
  LED1 = Infrared LED - 5mm [package="5 mm [THT]"]  # not connected
  DHT1 = DHT22 Humidity and Temperature Sensor

nets:
  3V3: U1.3V3, IR1.Vs, DHT1.VDD
  GND: U1.GND, IR1.GND, DHT1.GND

custom parts:
  ESP8266 NodeMCU LoLin module: ESP8266 based NodeMCU
  Infrared LED - 5mm: A generic infrared LED (~1.2V)
